// Logisim project simple_processor.circ as structural Verilog
module main (
);

  wire clk, rst;
  wire [2:0] undriven;
  wire [7:0] program_counter_q;
  wire [31:0] rom_1_data;

  Button start ();  // open: out
  Button u_clk (.out(clk));
  Button reset (.out(rst));
  // Probe on program_counter_q
  program_counter program_counter (.count(clk), .clk(clk), .reset(rst), .Q(program_counter_q));  // open: load, D
  cache cache (.clk(clk), .reset(rst));  // open: in, ld, addr, out
  ROM #(.dataWidth(32)) rom_1 (.addr(program_counter_q), .data(rom_1_data));  // open: sel
  // Probe on rom_1_data
  bus instruction_bus ();  // open: D_en, in, D, out
  registers reg_0_2 ();  // open: clk, reset, D, sel, reg_A, reg_B, reg_C
  bus mem_bus ();  // open: D_en, in, D, out
  ALU ALU (.OP(undriven));  // open: en, D0, D1, Q

  // Notes on the sheet:
  //   contents of rom_1 (hex, n*v repeats v):
  //   12 2 31
endmodule

module program_counter (
  input  load,
  input  [7:0] D,
  input  count,
  input  clk,
  input  reset,
  output [7:0] Q
);

  Counter counter_1 (.load(load), .D(D), .count(count), .Q(Q), .clk(clk), .clr(reset));  // open: carry
endmodule

module bus (
  input  D_en,
  input  [7:0] D,
  input  [7:0] in,
  output [7:0] out
);

  // Transmission_Gate #(.width(8)) transmission_1: pin names not known; wires that end beside it: D_en, D, in, D_en

  assign out = in;

  // Other names for the same wires on the sheet: Data_Ctrl = D_en
endmodule

module ALU (
  input  en,
  input  [2:0] OP,
  input  [7:0] D0,
  input  [7:0] D1,
  output [7:0] Q
);

  wire [7:0] adder_1_out, divider_1_out, multiplier_1_out, subtractor_1_out;

  Adder adder_1 (.a(D0), .b(D1), .out(adder_1_out));  // open: cin, cout
  Subtractor subtractor_1 (.a(D0), .b(D1), .out(subtractor_1_out));  // open: bin, bout
  Multiplier multiplier_1 (.a(D0), .b(D1), .out(multiplier_1_out));  // open: cin, cout
  Divider divider_1 (.a(D0), .b(D1), .out(divider_1_out));  // open: upper, rem
  BitAdder bitadder_1 ();  // open: in0, out
  Negator negator_1 ();  // open: in, out
  Comparator comparator_1 ();  // open: a, b, gt, eq, lt
  Shifter shifter_1 ();  // open: in, dist, out
  Multiplexer #(.select(3), .width(8)) multiplexer_1 (
    .in0(adder_1_out), .in1(subtractor_1_out), .in2(multiplier_1_out), .in3(divider_1_out), .out(Q),
    .sel(OP), .en(en));  // open: in4, in5, in6, in7
endmodule

module registers (
  input  clk,
  input  reset,
  input  [7:0] D,
  input  [1:0] sel,
  output [7:0] reg_A,
  output [7:0] reg_B,
  output [7:0] reg_C
);

  wire decoder_1_out0, decoder_1_out1, decoder_1_out2;

  Decoder #(.select(2), .enable("false")) decoder_1 (
    .out0(decoder_1_out0), .out1(decoder_1_out1), .out2(decoder_1_out2), .sel(sel));  // open: out3
  Register u_Reg_A (.D(D), .en(decoder_1_out0), .Q(reg_A), .clk(clk), .clr(reset));
  Register u_Reg_C (.D(D), .en(decoder_1_out1), .Q(reg_B), .clk(clk), .clr(reset));
  Register Reg_C_2 (.D(D), .en(decoder_1_out2), .Q(reg_C), .clk(clk), .clr(reset));

  // Notes on the sheet:
  //   TODO: clean up, have an en?
endmodule

module cache (
  input  [7:0] in,
  input  ld,
  input  [7:0] addr,
  input  clk,
  input  reset,
  output [7:0] out
);

  wire not_1_out;

  assign out = ld ? in : 8'bz;  // Controlled_Buffer controlled_buffer_1
  not not_1 (not_1_out, ld);
  RAM ram_1 (.addr(addr), .data(out), .clk(clk), .ld(not_1_out), .clr(reset));  // open: sel

  // Notes on the sheet:
  //   Reference: Logisim library documentation
endmodule

module ctrl (
  input  [19:0] instruction,
  output [3:0] opcode,
  output [3:0] Addr0,
  output [3:0] Addr1,
  output [7:0] val
);


  assign Addr0 = instruction[7:4];
  assign Addr1 = instruction[11:8];
  assign opcode = instruction[3:0];
  assign val = instruction[19:12];
endmodule
